// Logisim project first_proj.circ as structural Verilog: 30 circuits, main circuit main
module main (
  output [15:0] out_1,
  output [15:0] out_2,
  output [15:0] out_3,
  output [15:0] out_4,
  output [15:0] out_5,
  output [15:0] out_6,
  output [15:0] out_7,
  output [15:0] out_8,
  output [15:0] out_9,
  output [2:0] out_10,
  output [2:0] out_11,
  output [15:0] out_12,
  output [15:0] out_13
);

  wire a, alu_1_zero_f, and_1_out, B, button_1_out, c_1, C_J, clock_1_out, cmp_op_1_e, CMP_RUN,
       controlled_buffer_1_out, controlled_buffer_3_out, d_ff_2_q, IMM, J, LESS_I, LESS_O, NEW_OUT,
       not_1_out, not_2_out, not_3_out, not_4_out, not_5_out, not_6_out, not_7_out, not_8_out, not_10_out,
       not_11_out, not_12_out, not_13_out, not_14_out, not_15_out, op_hendeling_1_run_alu, or_1_out,
       or_2_out, or_3_out, PUSH_DATA, R, SIGN_I, SIGN_O, W, ZERO_I, ZERO_O;
  wire [2:0] REG_2;
  wire [3:0] zero_check_1_four, zero_check_1_one, zero_check_1_three, zero_check_1_two;
  wire [15:0] OUT_FROM_ALU, register_1_q, register_2_q, rom_read_1_address;

  or or_1 (or_1_out, IMM, J);
  not not_1 (not_1_out, c_1);
  assign controlled_buffer_1_out = or_1_out ? not_1_out : 1'bz;  // Controlled_Buffer controlled_buffer_1
  assign controlled_buffer_1_out = not_2_out ? c_1 : 1'bz;  // Controlled_Buffer controlled_buffer_2
  not not_2 (not_2_out, or_1_out);
  or or_2 (or_2_out, B, CMP_RUN);
  not not_3 (not_3_out, controlled_buffer_1_out);
  Button button_1 (.out(button_1_out));
  not not_4 (not_4_out, c_1);
  assign controlled_buffer_3_out = or_2_out ? not_4_out : 1'bz;  // Controlled_Buffer controlled_buffer_3
  assign controlled_buffer_3_out = not_5_out ? c_1 : 1'bz;  // Controlled_Buffer controlled_buffer_4
  not not_5 (not_5_out, or_2_out);
  not not_6 (not_6_out, R);
  assign out_6 = not_6_out ? OUT_FROM_ALU : 16'bz;  // Controlled_Buffer controlled_buffer_5
  assign out_6 = R ? out_3 : 16'bz;  // Controlled_Buffer controlled_buffer_6
  not not_7 (not_7_out, or_2_out);
  not not_8 (not_8_out, C_J);
  and and_1 (and_1_out, not_7_out, not_8_out, not_10_out);
  Clock clock_1 (.out(clock_1_out));
  not not_9 (c_1, clock_1_out);
  not not_10 (not_10_out, IMM);
  ROM #(.addrWidth(16), .dataWidth(16)) rom_1 (.addr(rom_read_1_address), .data(out_13));
  ROM_READ rom_read_1 (
    .C_ADDRESS(out_5), .N_ADDRESS(J), .NEW_READ(not_3_out), .RESET(button_1_out), .ADDRESS(rom_read_1_address));
  Register #(.width(16)) register_1 (.D(out_1), .en(NEW_OUT), .clk(c_1), .Q(register_1_q));  // open: clr
  not not_11 (not_11_out, controlled_buffer_3_out);
  or or_3 (or_3_out, PUSH_DATA, and_1_out);
  Hex_Digit_Display hex_digit_display_1 (.value(zero_check_1_four));  // open: dp
  Hex_Digit_Display hex_digit_display_2 (.value(zero_check_1_three));  // open: dp
  Hex_Digit_Display hex_digit_display_3 (.value(zero_check_1_two));  // open: dp
  Hex_Digit_Display hex_digit_display_4 (.value(zero_check_1_one));  // open: dp
  Flags_reg flags_reg_1 (
    .clock(c_1), .zero_I(ZERO_I), .sign_I(SIGN_I), .less_I(LESS_I), .zero_O(ZERO_O), .sign_O(SIGN_O),
    .less_O(LESS_O));
  registers registers_1 (
    .REG_2(REG_2), .REG_1(out_10), .clock(not_11_out), .store(or_3_out), .inpt(out_6), .REG_O_1(out_2),
    .REG_O_2(out_4));
  Register #(.width(16)) register_2 (
    .D(out_13), .en(not_12_out), .clk(not_13_out),
    .Q({register_2_q[15:11], REG_2, register_2_q[7], out_10, register_2_q[3:0]}));  // open: clr
  not not_12 (not_12_out, IMM);
  not not_13 (not_13_out, c_1);
  not not_14 (not_14_out, c_1);
  D_Flip_Flop d_ff_1 (.Q(B), .preset(register_2_q[7]), .reset(c_1));  // open: D, clk, Qn
  ZERO_CHECK zero_check_1 (
    .I(register_1_q), .FOUR(zero_check_1_four), .THREE(zero_check_1_three), .TWO(zero_check_1_two),
    .ONE(zero_check_1_one));  // open: zero_o
  and and_2 (IMM, register_2_q[7], not_14_out);
  _7_Segment_Display u_7_segment_display_1 ();  // open: g, f, a, b, e, d, c, dp
  // BCD_to_7_Segment_decoder bcd_to_7_segment_decoder_1: pin names not known
  // Binary_to_BCD_converter #(.binvalue(16)) binary_to_bcd_converter_1: pin names not known; wires that end beside it: register_1_q
  RAM #(.addrWidth(16), .dataWidth(16)) ram_1 (.addr(out_5), .we(W), .oe(R), .clk(c_1), .din(out_1), .dout(out_3));
  _7_Segment_Display u_7_segment_display_2 ();  // open: g, f, a, b, e, d, c, dp
  _7_Segment_Display u_7_segment_display_3 ();  // open: g, f, a, b, e, d, c, dp
  // BCD_to_7_Segment_decoder bcd_to_7_segment_decoder_2: pin names not known
  // BCD_to_7_Segment_decoder bcd_to_7_segment_decoder_3: pin names not known
  _7_Segment_Display u_7_segment_display_4 ();  // open: g, f, a, b, e, d, c, dp
  // BCD_to_7_Segment_decoder bcd_to_7_segment_decoder_4: pin names not known
  ARGS args_1 (.REG_1(out_2), .REG_2(out_4), .IMM_VAL(out_13), .IS_IMM(IMM), .ARG_1(out_1), .ARG_2(out_5));
  ALU alu_1 (
    .OP(out_11), .I_1(out_1), .I_2(out_5), .PUSH_DATA(PUSH_DATA), .O(OUT_FROM_ALU), .ZERO_F(alu_1_zero_f),
    .NEG_F(SIGN_I));
  _7_Segment_Display u_7_segment_display_5 ();  // open: g, f, a, b, e, d, c, dp
  // BCD_to_7_Segment_decoder bcd_to_7_segment_decoder_5: pin names not known
  OP_HENDELING op_hendeling_1 (
    .I_OP(register_2_q[3:0]), .ZERO_F(ZERO_O), .SIGN_F(SIGN_O), .LESS_F(LESS_O), .O_OP(out_11),
    .RUN_ALU(op_hendeling_1_run_alu), .WRITE(W), .READ(R), .CMP(CMP_RUN), .J(a), .C_J(C_J),
    .New_OUTPUT(NEW_OUT));
  not not_15 (not_15_out, CMP_RUN);
  assign ZERO_I = not_15_out ? alu_1_zero_f : 1'bz;  // Controlled_Buffer controlled_buffer_7
  and and_3 (PUSH_DATA, op_hendeling_1_run_alu, c_1);
  D_Flip_Flop d_ff_2 (.Q(d_ff_2_q), .preset(a), .reset(c_1));  // open: D, clk, Qn
  and and_4 (J, a, d_ff_2_q);
  assign ZERO_I = CMP_RUN ? cmp_op_1_e : 1'bz;  // Controlled_Buffer controlled_buffer_8
  CMP_OP cmp_op_1 (.I_1(out_5), .I_2(out_1), .RUN(CMP_RUN), .CLOCK(c_1), .E(cmp_op_1_e), .S(LESS_I));

  assign out_7 = out_6;
  assign out_8 = out_6;
  assign out_9 = out_4;
  assign out_12 = out_5;

  // Other names for the same wires on the sheet: ARG_1[15:0] = out_1; ARG_2[15:0] = out_5; IMM_VAL[15:0] = out_13;
  //   OP[2:0] = out_11; OUT_FROM_RAM[15:0] = out_3; REG_1[2:0] = out_10; REG_1_O[15:0] = out_2; REG_2_O[15:0] = out_4

  // Notes on the sheet:
  //   contents of rom_1 (hex, n*v repeats v):
  //   0 f0 ffff 760 90 18 a0 0 b0 1 9d 0 88 15 240 320 432 93 1 8a a 2f
endmodule

module Cadder (
  input  one,
  input  two,
  input  carry_in,
  output carry,
  output sum
);

  wire and_1_out, and_2_out, xor_1_out;

  and and_1 (and_1_out, one, two);
  xor xor_1 (xor_1_out, one, two);
  and and_2 (and_2_out, xor_1_out, carry_in);
  xor xor_2 (sum, xor_1_out, carry_in);
  or or_1 (carry, and_1_out, and_2_out);
endmodule

module four_bit_adder (
  input  eight_i_2,
  input  eight_i_1,
  input  four_i_2,
  input  four_i_1,
  input  two_i_2,
  input  two_i_1,
  input  one_i_2,
  input  one_i_1,
  input  carry_in,
  output carry_o,
  output eight_o,
  output four_o,
  output two_o,
  output one_o
);

  wire cadder_1_carry, cadder_2_carry, cadder_3_carry;

  Cadder cadder_1 (.one(one_i_2), .two(one_i_1), .carry_in(carry_in), .carry(cadder_1_carry), .sum(one_o));
  Cadder cadder_2 (.one(two_i_2), .two(two_i_1), .carry_in(cadder_1_carry), .carry(cadder_2_carry), .sum(two_o));
  Cadder cadder_3 (.one(four_i_2), .two(four_i_1), .carry_in(cadder_2_carry), .carry(cadder_3_carry), .sum(four_o));
  Cadder cadder_4 (.one(eight_i_2), .two(eight_i_1), .carry_in(cadder_3_carry), .carry(carry_o), .sum(eight_o));
endmodule

module sixteen_bit_adder (
  input  [15:0] I_2,
  input  [15:0] I_1,
  input  carry_i,
  output OVERFLOW,
  output [15:0] out_5
);

  wire and_1_out, and_2_out, four_bit_adder_1_carry_o, four_bit_adder_2_carry_o, four_bit_adder_3_carry_o,
       four_bit_adder_4_carry_o, not_1_out, not_2_out;

  // NoConnect on I_1[3]
  // NoConnect on I_1[3]
  four_bit_adder four_bit_adder_1 (
    .eight_i_2(I_2[3]), .eight_i_1(I_1[3]), .four_i_2(I_2[2]), .four_i_1(I_1[2]), .two_i_2(I_2[1]),
    .two_i_1(I_1[1]), .one_i_2(I_2[0]), .one_i_1(I_1[0]), .carry_in(carry_i),
    .carry_o(four_bit_adder_1_carry_o), .eight_o(out_5[3]), .four_o(out_5[2]), .two_o(out_5[1]),
    .one_o(out_5[0]));
  four_bit_adder four_bit_adder_2 (
    .eight_i_2(I_2[7]), .eight_i_1(I_1[7]), .four_i_2(I_2[6]), .four_i_1(I_1[6]), .two_i_2(I_2[5]),
    .two_i_1(I_1[5]), .one_i_2(I_2[4]), .one_i_1(I_1[4]), .carry_in(four_bit_adder_1_carry_o),
    .carry_o(four_bit_adder_2_carry_o), .eight_o(out_5[7]), .four_o(out_5[6]), .two_o(out_5[5]),
    .one_o(out_5[4]));
  four_bit_adder four_bit_adder_3 (
    .eight_i_2(I_2[11]), .eight_i_1(I_1[11]), .four_i_2(I_2[10]), .four_i_1(I_1[10]), .two_i_2(I_2[9]),
    .two_i_1(I_1[9]), .one_i_2(I_2[8]), .one_i_1(I_1[8]), .carry_in(four_bit_adder_2_carry_o),
    .carry_o(four_bit_adder_3_carry_o), .eight_o(out_5[11]), .four_o(out_5[10]), .two_o(out_5[9]),
    .one_o(out_5[8]));
  four_bit_adder four_bit_adder_4 (
    .eight_i_2(I_2[15]), .eight_i_1(I_1[15]), .four_i_2(I_2[14]), .four_i_1(I_1[14]), .two_i_2(I_2[13]),
    .two_i_1(I_1[13]), .one_i_2(I_2[12]), .one_i_1(I_1[12]), .carry_in(four_bit_adder_3_carry_o),
    .carry_o(four_bit_adder_4_carry_o), .eight_o(out_5[15]), .four_o(out_5[14]), .two_o(out_5[13]),
    .one_o(out_5[12]));
  not not_1 (not_1_out, I_2[15]);
  and and_1 (and_1_out, not_1_out, not_2_out);
  not not_2 (not_2_out, I_1[15]);
  and and_2 (and_2_out, out_5[15], and_1_out);
  or or_1 (OVERFLOW, four_bit_adder_4_carry_o, and_2_out);
endmodule

module register_1_bit (
  input  data,
  input  store,
  input  clock,
  output O
);

  wire and_1_out, and_2_out, not_1_out, or_1_out;

  not not_1 (not_1_out, store);
  and and_1 (and_1_out, data, store);
  and and_2 (and_2_out, O, not_1_out);
  or or_1 (or_1_out, and_2_out, and_1_out);
  D_flipFlop d_flipflop_1 (.data(or_1_out), .clock(clock), .o(O));
endmodule

module D_latch (
  input  store,
  input  data,
  output o
);

  wire and_1_out, and_2_out, nor_2_out, not_1_out;

  not not_1 (not_1_out, data);
  and and_1 (and_1_out, store, data);
  and and_2 (and_2_out, store, not_1_out);
  nor nor_1 (o, nor_2_out, and_2_out);
  nor nor_2 (nor_2_out, and_1_out, o);
endmodule

module D_flipFlop (
  input  data,
  input  clock,
  output o
);

  wire d_latch_1_o, not_1_out;

  not not_1 (not_1_out, clock);
  D_latch d_latch_1 (.store(not_1_out), .data(data), .o(d_latch_1_o));
  D_latch d_latch_2 (.store(clock), .data(d_latch_1_o), .o(o));
endmodule

module register_16_bit (
  input  [15:0] I,
  input  store,
  input  clock,
  output [15:0] O
);

  register_1_bit register_1_bit_1 (.data(I[15]), .store(store), .clock(clock), .O(O[15]));
  register_1_bit register_1_bit_2 (.data(I[14]), .store(store), .clock(clock), .O(O[14]));
  register_1_bit register_1_bit_3 (.data(I[13]), .store(store), .clock(clock), .O(O[13]));
  register_1_bit register_1_bit_4 (.data(I[12]), .store(store), .clock(clock), .O(O[12]));
  register_1_bit register_1_bit_5 (.data(I[11]), .store(store), .clock(clock), .O(O[11]));
  register_1_bit register_1_bit_6 (.data(I[10]), .store(store), .clock(clock), .O(O[10]));
  register_1_bit register_1_bit_7 (.data(I[9]), .store(store), .clock(clock), .O(O[9]));
  register_1_bit register_1_bit_8 (.data(I[8]), .store(store), .clock(clock), .O(O[8]));
  register_1_bit register_1_bit_9 (.data(I[7]), .store(store), .clock(clock), .O(O[7]));
  register_1_bit register_1_bit_10 (.data(I[6]), .store(store), .clock(clock), .O(O[6]));
  register_1_bit register_1_bit_11 (.data(I[5]), .store(store), .clock(clock), .O(O[5]));
  register_1_bit register_1_bit_12 (.data(I[4]), .store(store), .clock(clock), .O(O[4]));
  register_1_bit register_1_bit_13 (.data(I[3]), .store(store), .clock(clock), .O(O[3]));
  register_1_bit register_1_bit_14 (.data(I[2]), .store(store), .clock(clock), .O(O[2]));
  register_1_bit register_1_bit_15 (.data(I[1]), .store(store), .clock(clock), .O(O[1]));
  register_1_bit register_1_bit_16 (.data(I[0]), .store(store), .clock(clock), .O(O[0]));
  Hex_Digit_Display hex_digit_display_1 (.value(O[15:12]));  // open: dp
  Hex_Digit_Display hex_digit_display_2 (.value(O[11:8]));  // open: dp
  Hex_Digit_Display hex_digit_display_3 (.value(O[7:4]));  // open: dp
  Hex_Digit_Display hex_digit_display_4 (.value(O[3:0]));  // open: dp
endmodule

module registers (
  input  [15:0] inpt,
  input  clock,
  input  store,
  input  [2:0] REG_1,
  input  [2:0] REG_2,
  output [15:0] REG_O_1,
  output [15:0] REG_O_2
);

  wire and_1_out, and_2_out, and_3_out, and_4_out, and_5_out, and_6_out, and_7_out, and_8_out,
       choose_reg_1_five, choose_reg_1_four, choose_reg_1_one, choose_reg_1_seven, choose_reg_1_six,
       choose_reg_1_three, choose_reg_1_two, choose_reg_1_zero;
  wire [15:0] bp_q, r0_q, r1_q, r2_q, r3_q, r4_q, r5_q, sp_q;

  and and_1 (and_1_out, store, choose_reg_1_seven);
  and and_2 (and_2_out, choose_reg_1_five, store);
  and and_3 (and_3_out, choose_reg_1_six, store);
  choose_reg choose_reg_1 (
    .op(REG_1), .zero(choose_reg_1_zero), .one(choose_reg_1_one), .two(choose_reg_1_two),
    .three(choose_reg_1_three), .four(choose_reg_1_four), .five(choose_reg_1_five), .six(choose_reg_1_six),
    .seven(choose_reg_1_seven));
  and and_4 (and_4_out, store, choose_reg_1_four);
  and and_5 (and_5_out, store, choose_reg_1_three);
  and and_6 (and_6_out, store, choose_reg_1_two);
  and and_7 (and_7_out, choose_reg_1_one, store);
  and and_8 (and_8_out, choose_reg_1_zero, store);
  Register #(.width(16)) r0 (.D(inpt), .en(and_8_out), .clk(clock), .Q(r0_q));  // open: clr
  Register #(.width(16)) r1 (.D(inpt), .en(and_7_out), .clk(clock), .Q(r1_q));  // open: clr
  Register #(.width(16)) r2 (.D(inpt), .en(and_6_out), .clk(clock), .Q(r2_q));  // open: clr
  Register #(.width(16)) r3 (.D(inpt), .en(and_5_out), .clk(clock), .Q(r3_q));  // open: clr
  Register #(.width(16)) r4 (.D(inpt), .en(and_4_out), .clk(clock), .Q(r4_q));  // open: clr
  Register #(.width(16)) r5 (.D(inpt), .en(and_2_out), .clk(clock), .Q(r5_q));  // open: clr
  Register #(.width(16)) bp (.D(inpt), .en(and_3_out), .clk(clock), .Q(bp_q));  // open: clr
  Register #(.width(16)) sp (.D(inpt), .en(and_1_out), .clk(clock), .Q(sp_q));  // open: clr
  Reg_to_bus reg_to_bus_1 (
    .zero(r0_q), .one(r1_q), .two(r2_q), .three(r3_q), .four(r4_q), .five(r5_q), .six(bp_q), .seven(sp_q),
    .ID(REG_1), .O(REG_O_1));
  Reg_to_bus reg_to_bus_2 (
    .zero(r0_q), .one(r1_q), .two(r2_q), .three(r3_q), .four(r4_q), .five(r5_q), .six(bp_q), .seven(sp_q),
    .ID(REG_2), .O(REG_O_2));

  // Other names for the same wires on the sheet: ID[2:0] = REG_1
endmodule

module choose_reg (
  input  [2:0] op,
  output zero,
  output one,
  output two,
  output three,
  output four,
  output five,
  output six,
  output seven
);

  wire and_2_out, and_4_out, and_6_out, and_8_out, not_1_out, not_2_out, not_3_out;

  and and_1 (zero, and_2_out, not_1_out);
  and and_2 (and_2_out, not_3_out, not_2_out);
  and and_3 (one, and_4_out, not_1_out);
  and and_4 (and_4_out, op[0], not_2_out);
  and and_5 (two, and_6_out, not_1_out);
  and and_6 (and_6_out, not_3_out, op[1]);
  and and_7 (three, and_8_out, not_1_out);
  and and_8 (and_8_out, op[0], op[1]);
  and and_9 (four, and_2_out, op[2]);
  and and_10 (five, and_4_out, op[2]);
  and and_11 (six, and_6_out, op[2]);
  not not_1 (not_1_out, op[2]);
  not not_2 (not_2_out, op[1]);
  not not_3 (not_3_out, op[0]);
  and and_12 (seven, and_8_out, op[2]);
endmodule

module Or_Op (
  input  [15:0] I_1,
  input  [15:0] I_2,
  output [15:0] O
);

  assign O = I_1 | I_2;  // OR_Gate or_1, 16 bits wide
endmodule

module Base_Num_S (
  input  [3:0] in_1,
  input  p,
  output [3:0] out_3,
  output T
);

  assign out_3[0] = T ? in_1[0] : 1'bz;  // Controlled_Buffer controlled_buffer_1
  assign out_3[1] = T ? in_1[1] : 1'bz;  // Controlled_Buffer controlled_buffer_2
  assign out_3[2] = T ? in_1[2] : 1'bz;  // Controlled_Buffer controlled_buffer_3
  assign out_3[3] = T ? in_1[3] : 1'bz;  // Controlled_Buffer controlled_buffer_4
  or or_1 (T, in_1[0], in_1[1], p, in_1[2], in_1[3]);
endmodule

module Reg_to_bus (
  input  [15:0] zero,
  input  [15:0] one,
  input  [15:0] two,
  input  [15:0] three,
  input  [15:0] four,
  input  [15:0] five,
  input  [15:0] six,
  input  [15:0] seven,
  input  [2:0] ID,
  output [15:0] O
);

  wire choose_reg_1_five, choose_reg_1_four, choose_reg_1_one, choose_reg_1_seven, choose_reg_1_six,
       choose_reg_1_three, choose_reg_1_two, choose_reg_1_zero;

  choose_reg choose_reg_1 (
    .op(ID), .zero(choose_reg_1_zero), .one(choose_reg_1_one), .two(choose_reg_1_two),
    .three(choose_reg_1_three), .four(choose_reg_1_four), .five(choose_reg_1_five), .six(choose_reg_1_six),
    .seven(choose_reg_1_seven));
  BUFFER_16bit buffer_16bit_1 (.i(zero), .choose(choose_reg_1_zero), .o(O));
  BUFFER_16bit buffer_16bit_2 (.i(one), .choose(choose_reg_1_one), .o(O));
  BUFFER_16bit buffer_16bit_3 (.i(two), .choose(choose_reg_1_two), .o(O));
  BUFFER_16bit buffer_16bit_4 (.i(three), .choose(choose_reg_1_three), .o(O));
  BUFFER_16bit buffer_16bit_5 (.i(four), .choose(choose_reg_1_four), .o(O));
  BUFFER_16bit buffer_16bit_6 (.i(five), .choose(choose_reg_1_five), .o(O));
  BUFFER_16bit buffer_16bit_7 (.i(six), .choose(choose_reg_1_six), .o(O));
  BUFFER_16bit buffer_16bit_8 (.i(seven), .choose(choose_reg_1_seven), .o(O));
endmodule

module BUFFER_16bit (
  input  [15:0] i,
  input  choose,
  output [15:0] o
);

  assign o[0] = choose ? i[0] : 1'bz;  // Controlled_Buffer controlled_buffer_1
  assign o[1] = choose ? i[1] : 1'bz;  // Controlled_Buffer controlled_buffer_2
  assign o[2] = choose ? i[2] : 1'bz;  // Controlled_Buffer controlled_buffer_3
  assign o[3] = choose ? i[3] : 1'bz;  // Controlled_Buffer controlled_buffer_4
  assign o[4] = choose ? i[4] : 1'bz;  // Controlled_Buffer controlled_buffer_5
  assign o[5] = choose ? i[5] : 1'bz;  // Controlled_Buffer controlled_buffer_6
  assign o[6] = choose ? i[6] : 1'bz;  // Controlled_Buffer controlled_buffer_7
  assign o[7] = choose ? i[7] : 1'bz;  // Controlled_Buffer controlled_buffer_8
  assign o[8] = choose ? i[8] : 1'bz;  // Controlled_Buffer controlled_buffer_9
  assign o[9] = choose ? i[9] : 1'bz;  // Controlled_Buffer controlled_buffer_10
  assign o[10] = choose ? i[10] : 1'bz;  // Controlled_Buffer controlled_buffer_11
  assign o[11] = choose ? i[11] : 1'bz;  // Controlled_Buffer controlled_buffer_12
  assign o[12] = choose ? i[12] : 1'bz;  // Controlled_Buffer controlled_buffer_13
  assign o[13] = choose ? i[13] : 1'bz;  // Controlled_Buffer controlled_buffer_14
  assign o[14] = choose ? i[14] : 1'bz;  // Controlled_Buffer controlled_buffer_15
  assign o[15] = choose ? i[15] : 1'bz;  // Controlled_Buffer controlled_buffer_16
endmodule

module ALU (
  input  [15:0] I_1,
  input  [15:0] I_2,
  input  PUSH_DATA,
  input  [2:0] OP,
  output NEG_F,
  output ZERO_F,
  output [15:0] O
);

  wire [2:0] zero_check_2_four;
  wire [3:0] zero_check_1_four, zero_check_1_one, zero_check_1_three, zero_check_1_two, zero_check_2_one,
       zero_check_2_three, zero_check_2_two;
  wire [15:0] mov_op_1_o, not_op_1_o, or_op_1_o, set_alu_out_1_o, shl_op_1_o, shr_op_1_o,
       sixteen_bit_adder_1_out_5, sub_op_1_sum, xor_op_1_o;

  MOV_OP mov_op_1 (.I_1(I_2), .O(mov_op_1_o));
  Xor_op xor_op_1 (.I_1(I_1), .I_2(I_2), .O(xor_op_1_o));
  sixteen_bit_adder sixteen_bit_adder_1 (
    .I_1(I_1), .I_2(I_2), .out_5(sixteen_bit_adder_1_out_5));  // open: carry_i, OVERFLOW
  sub_op sub_op_1 (.I_2(I_2), .I_1(I_1), .SUM(sub_op_1_sum));  // open: OVERFLOW_F, CARRY_F
  SHL_OP shl_op_1 (.I_1(I_1), .O(shl_op_1_o));
  SHR_OP shr_op_1 (.I_1(I_1), .O(shr_op_1_o));
  Not_op not_op_1 (.I_1(I_1), .O(not_op_1_o));
  Or_Op or_op_1 (.I_1(I_1), .I_2(I_2), .O(or_op_1_o));
  Hex_Digit_Display hex_digit_display_1 (.value(zero_check_1_four));  // open: dp
  Hex_Digit_Display hex_digit_display_2 (.value(zero_check_1_three));  // open: dp
  set_ALU_out set_alu_out_1 (
    .MOV_I(mov_op_1_o), .XOR_I(xor_op_1_o), .ADD_I(sixteen_bit_adder_1_out_5), .SUB_I(sub_op_1_sum),
    .SHL_I(shl_op_1_o), .SHR_I(shr_op_1_o), .NOT_I(not_op_1_o), .OR_I(or_op_1_o), .OP(OP), .O(set_alu_out_1_o));
  Hex_Digit_Display hex_digit_display_3 (.value(zero_check_1_two));  // open: dp
  Hex_Digit_Display hex_digit_display_4 (.value(zero_check_1_one));  // open: dp
  ZERO_CHECK zero_check_1 (
    .I(set_alu_out_1_o), .FOUR(zero_check_1_four), .THREE(zero_check_1_three), .TWO(zero_check_1_two),
    .ONE(zero_check_1_one));  // open: zero_o
  Register #(.width(16)) register_1 (.D(set_alu_out_1_o), .en(1'b1), .clk(PUSH_DATA), .Q(O));  // open: clr
  Hex_Digit_Display hex_digit_display_5 (.value({NEG_F, zero_check_2_four}));  // open: dp
  Hex_Digit_Display hex_digit_display_6 (.value(zero_check_2_three));  // open: dp
  Hex_Digit_Display hex_digit_display_7 (.value(zero_check_2_two));  // open: dp
  Hex_Digit_Display hex_digit_display_8 (.value(zero_check_2_one));  // open: dp
  ZERO_CHECK zero_check_2 (
    .I(O), .FOUR({NEG_F, zero_check_2_four}), .THREE(zero_check_2_three), .TWO(zero_check_2_two),
    .ONE(zero_check_2_one), .zero_o(ZERO_F));
endmodule

module choose_op (
  input  [2:0] in_1,
  output MOV_O,
  output XOR_OP,
  output ADD_OP,
  output SUB_OP,
  output SHL_OP,
  output SHR_OP,
  output NOT_OP,
  output OR_OP
);

  wire and_1_out, and_2_out, and_3_out, and_4_out;
  wire [2:0] not_1_out;

  assign not_1_out = ~in_1;  // NOT_Gate not_1, 3 bits wide
  and and_1 (and_1_out, not_1_out[0], not_1_out[1]);
  and and_2 (and_2_out, in_1[0], not_1_out[1]);
  and and_3 (and_3_out, not_1_out[0], in_1[1]);
  and and_4 (and_4_out, in_1[0], in_1[1]);
  and and_5 (MOV_O, and_1_out, not_1_out[2]);
  and and_6 (XOR_OP, not_1_out[2], and_2_out);
  and and_7 (ADD_OP, not_1_out[2], and_3_out);
  and and_8 (SUB_OP, not_1_out[2], and_4_out);
  and and_9 (SHL_OP, and_1_out, in_1[2]);
  and and_10 (SHR_OP, in_1[2], and_2_out);
  and and_11 (NOT_OP, in_1[2], and_3_out);
  and and_12 (OR_OP, in_1[2], and_4_out);
endmodule

module sub_op (
  input  [15:0] I_1,
  input  [15:0] I_2,
  output CARRY_F,
  output [15:0] SUM,
  output OVERFLOW_F
);

  wire [3:0] zero_check_1_four, zero_check_1_one, zero_check_1_three, zero_check_1_two;
  wire [15:0] xor_1_out;

  assign xor_1_out = I_2 ^ {16{1'b1}};  // XOR_Gate xor_1, 16 bits wide
  sixteen_bit_adder sixteen_bit_adder_1 (
    .I_1(xor_1_out), .carry_i(1'b1), .I_2(I_1), .out_5(SUM), .OVERFLOW(OVERFLOW_F));
  Hex_Digit_Display hex_digit_display_1 (.value(zero_check_1_four));  // open: dp
  Hex_Digit_Display hex_digit_display_2 (.value(zero_check_1_three));  // open: dp
  ZERO_CHECK zero_check_1 (
    .I(SUM), .FOUR(zero_check_1_four), .THREE(zero_check_1_three), .TWO(zero_check_1_two),
    .ONE(zero_check_1_one));  // open: zero_o
  Hex_Digit_Display hex_digit_display_3 (.value(zero_check_1_one));  // open: dp
  Hex_Digit_Display hex_digit_display_4 (.value(zero_check_1_two));  // open: dp
endmodule

module set_ALU_out (
  input  [15:0] MOV_I,
  input  [15:0] XOR_I,
  input  [15:0] ADD_I,
  input  [15:0] SUB_I,
  input  [15:0] SHL_I,
  input  [15:0] SHR_I,
  input  [15:0] NOT_I,
  input  [15:0] OR_I,
  input  [2:0] OP,
  output [15:0] O
);

  wire choose_op_1_add_op, choose_op_1_mov_o, choose_op_1_not_op, choose_op_1_or_op, choose_op_1_shl_op,
       choose_op_1_shr_op, choose_op_1_sub_op, choose_op_1_xor_op;

  choose_op choose_op_1 (
    .in_1(OP), .MOV_O(choose_op_1_mov_o), .XOR_OP(choose_op_1_xor_op), .ADD_OP(choose_op_1_add_op),
    .SUB_OP(choose_op_1_sub_op), .SHL_OP(choose_op_1_shl_op), .SHR_OP(choose_op_1_shr_op),
    .NOT_OP(choose_op_1_not_op), .OR_OP(choose_op_1_or_op));
  BUFFER_16bit buffer_16bit_1 (.i(MOV_I), .choose(choose_op_1_mov_o), .o(O));
  BUFFER_16bit buffer_16bit_2 (.i(XOR_I), .choose(choose_op_1_xor_op), .o(O));
  BUFFER_16bit buffer_16bit_3 (.i(ADD_I), .choose(choose_op_1_add_op), .o(O));
  BUFFER_16bit buffer_16bit_4 (.i(SUB_I), .choose(choose_op_1_sub_op), .o(O));
  BUFFER_16bit buffer_16bit_5 (.i(SHL_I), .choose(choose_op_1_shl_op), .o(O));
  BUFFER_16bit buffer_16bit_6 (.i(SHR_I), .choose(choose_op_1_shr_op), .o(O));
  BUFFER_16bit buffer_16bit_7 (.i(NOT_I), .choose(choose_op_1_not_op), .o(O));
  BUFFER_16bit buffer_16bit_8 (.i(OR_I), .choose(choose_op_1_or_op), .o(O));
endmodule

module Xor_op (
  input  [15:0] I_1,
  input  [15:0] I_2,
  output [15:0] O
);

  assign O = I_1 ^ I_2;  // XOR_Gate xor_1, 16 bits wide
endmodule

module ZERO_CHECK (
  input  [15:0] I,
  output [3:0] FOUR,
  output [3:0] THREE,
  output [3:0] TWO,
  output [3:0] ONE,
  output zero_o
);

  wire base_num_s_1_t, base_num_s_2_t, base_num_s_3_t;
  wire [15:0] not_1_out;

  assign not_1_out = ~I;  // NOT_Gate not_1, 16 bits wide
  and and_1 (zero_o, not_1_out[0], not_1_out[1], not_1_out[2], not_1_out[3], not_1_out[4], not_1_out[5], not_1_out[6], not_1_out[7], not_1_out[8], not_1_out[9], not_1_out[10], not_1_out[11], not_1_out[12], not_1_out[13], not_1_out[14], not_1_out[15]);
  Base_Num_S base_num_s_1 (.in_1(I[15:12]), .out_3(FOUR), .T(base_num_s_1_t));  // open: p
  Base_Num_S base_num_s_2 (.in_1(I[11:8]), .p(base_num_s_1_t), .out_3(THREE), .T(base_num_s_2_t));
  Base_Num_S base_num_s_3 (.in_1(I[7:4]), .p(base_num_s_2_t), .out_3(TWO), .T(base_num_s_3_t));
  Base_Num_S base_num_s_4 (.in_1(I[3:0]), .p(base_num_s_3_t), .out_3(ONE));  // open: T
endmodule

module SHL_OP (
  input  [15:0] I_1,
  output [15:0] O
);


  assign O = {1'b0, I_1[15:1]};
endmodule

module SHR_OP (
  input  [15:0] I_1,
  output [15:0] O
);


  assign O = {I_1[14:0], 1'b0};
endmodule

module Not_op (
  input  [15:0] I_1,
  output [15:0] O
);

  assign O = ~I_1;  // NOT_Gate not_1, 16 bits wide
endmodule

module MOV_OP (
  input  [15:0] I_1,
  output [15:0] O
);


  assign O = I_1;
endmodule

module Flags_reg (
  input  clock,
  input  zero_I,
  input  sign_I,
  input  less_I,
  output zero_O,
  output sign_O,
  output less_O
);

  Register #(.width(1)) register_1 (.D(zero_I), .en(1'b1), .clk(clock), .Q(zero_O));  // open: clr
  Register #(.width(1)) register_2 (.D(sign_I), .en(1'b1), .clk(clock), .Q(sign_O));  // open: clr
  Register #(.width(1)) register_3 (.D(less_I), .en(1'b1), .clk(1'b1), .Q(less_O));  // open: clr
endmodule

module OP_HENDELING (
  input  [3:0] I_OP,
  input  ZERO_F,
  input  SIGN_F,
  input  LESS_F,
  output [2:0] O_OP,
  output RUN_ALU,
  output WRITE,
  output READ,
  output CMP,
  output J,
  output C_J,
  output New_OUTPUT
);

  wire and_1_out, and_2_out, non_alu_ops_1_jl, non_alu_ops_1_jmp, non_alu_ops_1_js, non_alu_ops_1_jz;

  NON_ALU_OPS non_alu_ops_1 (
    .OP(I_OP), .JZ(non_alu_ops_1_jz), .JS(non_alu_ops_1_js), .jmp(non_alu_ops_1_jmp), .WRITE(WRITE),
    .READ(READ), .CMP(CMP), .JL(non_alu_ops_1_jl), .NEW_OUT(New_OUTPUT));
  and and_1 (and_1_out, ZERO_F, non_alu_ops_1_jz);
  and and_2 (and_2_out, non_alu_ops_1_js, SIGN_F);
  and and_3 (and_2_out, LESS_F, non_alu_ops_1_jl);
  or or_1 (J, and_1_out, non_alu_ops_1_jmp, and_2_out);
  not not_1 (RUN_ALU, I_OP[3]);
  or or_2 (C_J, non_alu_ops_1_jz, non_alu_ops_1_js, J);

  assign O_OP = I_OP[2:0];
endmodule

module ROM_READ (
  input  [15:0] C_ADDRESS,
  input  N_ADDRESS,
  input  NEW_READ,
  input  RESET,
  output [15:0] ADDRESS
);

  wire not_1_out;
  wire [15:0] adder_1_out, controlled_buffer_1_out;

  not not_1 (not_1_out, N_ADDRESS);
  assign controlled_buffer_1_out = N_ADDRESS ? C_ADDRESS : 16'bz;  // Controlled_Buffer controlled_buffer_1
  assign controlled_buffer_1_out = not_1_out ? adder_1_out : 16'bz;  // Controlled_Buffer controlled_buffer_2
  Register #(.width(16)) register_1 (.D(controlled_buffer_1_out), .en(1'b1), .clk(NEW_READ), .Q(ADDRESS), .clr(RESET));
  Adder #(.width(16)) adder_1 (.a(16'h1), .b(ADDRESS), .out(adder_1_out));  // open: cin, cout
endmodule

module ARGS (
  input  [15:0] REG_1,
  input  [15:0] REG_2,
  input  [15:0] IMM_VAL,
  input  IS_IMM,
  output [15:0] ARG_1,
  output [15:0] ARG_2
);

  wire not_1_out;

  assign ARG_2 = not_1_out ? REG_2 : 16'bz;  // Controlled_Buffer controlled_buffer_1
  assign ARG_2 = IS_IMM ? IMM_VAL : 16'bz;  // Controlled_Buffer controlled_buffer_2
  not not_1 (not_1_out, IS_IMM);

  assign ARG_1 = REG_1;
endmodule

module NON_ALU_OPS (
  input  [3:0] OP,
  output JZ,
  output JS,
  output jmp,
  output WRITE,
  output READ,
  output CMP,
  output JL,
  output NEW_OUT
);

  wire [3:0] not_1_out;

  assign not_1_out = ~OP;  // NOT_Gate not_1, 4 bits wide
  and and_1 (JZ, not_1_out[0], not_1_out[1], not_1_out[2], OP[3]);
  and and_2 (JS, OP[0], not_1_out[1], not_1_out[2], OP[3]);
  and and_3 (jmp, not_1_out[0], OP[1], not_1_out[2], OP[3]);
  and and_4 (WRITE, OP[0], OP[1], not_1_out[2], OP[3]);
  and and_5 (READ, not_1_out[0], not_1_out[1], OP[2], OP[3]);
  and and_6 (CMP, OP[3], OP[2], not_1_out[1], OP[0]);
  and and_7 (JL, not_1_out[0], OP[3], OP[2], OP[1]);
  and and_8 (NEW_OUT, OP[3], OP[2], OP[1], OP[0]);
endmodule

module CMP_OP (
  input  [15:0] I_1,
  input  [15:0] I_2,
  input  RUN,
  input  CLOCK,
  output E,
  output S
);

  Comparator #(.width(16)) comparator_1 (.a(I_1), .b(I_2), .eq(E), .lt(S));  // open: gt
endmodule
